# Fritzing sketch Serra (saved by Fritzing 0.9.10b)
circuit board: 9.34524cm x 5.6368cm
breadboards: 1

parts:
  Photoresistor = PHOTOCELL [package=photocell-kit]
  LED_strip = WS2812 RGB LED matrix 1x8
  Soil = Soil Moisture Sensor
  Water_Pump = water pump/motor  # not connected
  Switch = Taiway 100-SP-X-T1 SPDT Miniature Toggle Switch [part_number=100-SP-X-T1-0-0-B1-M1 package=THT]
  Fan1 = DC Motor [voltage_(max)=6V voltage_(min)=3V]
  Fan2 = DC Motor [voltage_(max)=6V voltage_(min)=3V]
  RelayPump = KY-019 5V Relay Module [package="Breakout board"]
  Part2 = Arduino Uno (Rev3)
  Res_photo = Resistor [tolerance=±5% power=0.25 resistance=220 package=THT]
  RelayFan2 = KY-019 5V Relay Module [package="Breakout board"]
  RelayFan1 = KY-019 5V Relay Module [package="Breakout board"]
  Temperature = Humidity and Temperature Sensor RHT03
  Res_LED = Resistor [tolerance=±5% power=0.25 resistance=220 package=THT]
  Display = Grove OLED 128x96

nets:
  VCC: Photoresistor.P$1, Soil.VCC, Switch.L2, Part2.5V, Temperature.Vcc, Display.VCC
  N1: Photoresistor.P$2, Part2.A2, Res_photo.Pin_1
  GND: LED_strip.GND, Soil.GND, Switch.COM, Part2.GND, Res_photo.Pin_0, Temperature.GND_1, Display.GND
  N2: LED_strip.VCC, Switch.L1
  N3: LED_strip.DIN, Res_LED.Pin_0
  N4: Soil.SIG, Part2.A1
  N5: Fan1.pin_1, RelayFan1.Common
  N6: Fan1.pin_2, RelayFan1.NO
  N7: Fan2.pin_1, RelayFan2.Common
  N8: Fan2.pin_2, RelayFan2.NO
  N9: RelayPump.S, Part2.D3_PWM
  N10: Part2.A3, Temperature.Data-signal
  N11: Part2.A4/SDA, Display.SDA
  N12: Part2.A5/SCL, Display.SCL
  N13: Part2.D13/SCK, RelayFan2.S, RelayFan1.S
  N14: Part2.D2, Res_LED.Pin_1

notes:
  switch
  vento
  Sensori
  Attuatori

custom parts:
  WS2812 RGB LED matrix 1x8: WS2812 matrix 1x8
  water pump/motor: WATER PUMP BY ARDUBLOCKTR
  KY-019 5V Relay Module: KY-019 5V Relay module, used to control AC circuits. (Special thanks to vanepp for fixing the PCB holes and other errors)

// code stored in the sketch: Serr.ino


// code stored in the sketch: Serra.ino
const int fanPin = 13; //(pin del relay connesso alle ventole)
const int ledPin = 2;
const int SCLPin = A5;
const int SDAPin = A4;
const int tempPin = A3;
const int photoPin = A2;
//const int soilPin = A1;
//const int waterPumpPin = 2;




void setup(){
	Serial.begin(115200);
   pinMode(fanPin, OUTPUT);
}

void fanON{
	digitalWrite(fanPin, HIGH);
}

int readTemperature{
	return analogRead(tempPin);


void loop(){
	Serial.println(readTemperature());
	delay(100);	



}
